// Logisim project Logisim.circ as structural Verilog
module main (
  input  Reset_PC,
  input  reset_cntroler,
  input  reset_reg_file,
  input  in_4,
  output [3:0] out_5,
  output [3:0] out_6
);

  wire branch_1_iftrue, clock_1_out, control_unit_1_active_mem, control_unit_1_jump, control_unit_1_load_mem,
       control_unit_1_loadalu, control_unit_1_mem_store, control_unit_1_pc_write, control_unit_1_read_en,
       control_unit_1_write_enable, data_splitter_1_branch_oper, data_splitter_1_imm_reg,
       data_splitter_1_ld_st, not_1_out;
  wire [2:0] data_splitter_1_n_z_p, data_splitter_1_opcode;
  wire [3:0] data_splitter_1_read_reg_1, data_splitter_1_read_reg_2, data_splitter_1_write_reg;
  wire [9:0] data_splitter_1_ldadress, data_splitter_1_st_adress, multiplexer_6_out;
  wire [17:0] alu_1_output, data_splitter_1_brach_adress, data_splitter_1_extended_imm_val,
       data_splitter_1_jump_adrress, multiplexer_1_out, multiplexer_2_out, multiplexer_3_out,
       multiplexer_4_out, multiplexer_5_out, multiplexer_7_out, multiplexer_8_out, n18_bit_adder_1_utput,
       n18_bit_adder_2_utput, pc_1_pcoutput, ram_1_data, register_file_1_readdata1,
       register_file_1_readdata2, rom_1_data;

  Multiplexer #(.width(18), .enable("false")) multiplexer_1 (
    .in0(data_splitter_1_jump_adrress), .in1(data_splitter_1_brach_adress), .out(multiplexer_1_out),
    .sel(data_splitter_1_branch_oper));
  not not_1 (not_1_out, 1'b1);
  _18_bit_adder u_18_bit_adder_1 (
    .c_in(not_1_out), .input_1(pc_1_pcoutput), .input_2(multiplexer_1_out), .utput(n18_bit_adder_1_utput));  // open: c_out
  _18_bit_adder u_18_bit_adder_2 (
    .c_in(1'b1), .input_1(pc_1_pcoutput), .input_2({18{1'b0}}), .utput(n18_bit_adder_2_utput));  // open: c_out
  Multiplexer #(.width(18), .enable("false")) multiplexer_2 (
    .in1(register_file_1_readdata2), .out(multiplexer_2_out), .sel(data_splitter_1_branch_oper));  // open: in0
  Multiplexer #(.width(18), .enable("false")) multiplexer_3 (
    .in1(register_file_1_readdata1), .out(multiplexer_3_out), .sel(data_splitter_1_branch_oper));  // open: in0
  Multiplexer #(.width(18), .enable("false")) multiplexer_4 (
    .in0(n18_bit_adder_2_utput), .in1(n18_bit_adder_1_utput), .out(multiplexer_4_out),
    .sel(control_unit_1_jump));
  PC pc_1 (
    .PCinDATA(multiplexer_4_out), .clear(Reset_PC), .loadEnable(control_unit_1_pc_write), .clck(clock_1_out),
    .PCoutput(pc_1_pcoutput));
  branch branch_1 (
    .nzp(data_splitter_1_n_z_p), .input_1(multiplexer_3_out), .input_2(multiplexer_2_out),
    .iftrue(branch_1_iftrue));
  Clock clock_1 (.out(clock_1_out));
  ROM #(.addrWidth(18), .dataWidth(18)) rom_1 (.addr(pc_1_pcoutput), .data(rom_1_data));  // open: sel
  data_splitter data_splitter_1 (
    .input_18bit(rom_1_data), .opcode(data_splitter_1_opcode), .write_reg(data_splitter_1_write_reg),
    .read_reg_1(data_splitter_1_read_reg_1), .imm_reg(data_splitter_1_imm_reg),
    .read_reg_2(data_splitter_1_read_reg_2), .extended_imm_val(data_splitter_1_extended_imm_val),
    .ldadress(data_splitter_1_ldadress), .st_adress(data_splitter_1_st_adress),
    .jump_adrress(data_splitter_1_jump_adrress), .n_z_p(data_splitter_1_n_z_p),
    .brach_adress(data_splitter_1_brach_adress), .ld_st(data_splitter_1_ld_st),
    .branch_oper(data_splitter_1_branch_oper));  // open: branch_or_jump
  Control_Unit control_unit_1 (
    .iftrue(branch_1_iftrue), .opcode(data_splitter_1_opcode), .pc_write(control_unit_1_pc_write),
    .loadALU(control_unit_1_loadalu), .write_enable(control_unit_1_write_enable),
    .mem_store(control_unit_1_mem_store), .active_mem(control_unit_1_active_mem),
    .read_en(control_unit_1_read_en), .clock(clock_1_out), .next(out_5), .current(out_6),
    .clear(reset_cntroler), .load_mem(control_unit_1_load_mem), .jump(control_unit_1_jump));  // open: fetch
  Register_file register_file_1 (
    .writeData(multiplexer_5_out), .writeAdress(data_splitter_1_write_reg),
    .writeEnable(control_unit_1_write_enable), .clck(clock_1_out), .clear(reset_reg_file),
    .readDATA1(register_file_1_readdata1), .readDATA2(register_file_1_readdata2),
    .readEN(control_unit_1_read_en), .readADD1(data_splitter_1_read_reg_1),
    .readADD2(data_splitter_1_read_reg_2));
  Multiplexer #(.width(18), .enable("false")) multiplexer_5 (
    .in0(alu_1_output), .in1(ram_1_data), .out(multiplexer_5_out), .sel(data_splitter_1_opcode[2]));
  Multiplexer #(.width(10), .enable("false")) multiplexer_6 (
    .in0(data_splitter_1_ldadress), .in1(data_splitter_1_st_adress), .out(multiplexer_6_out),
    .sel(data_splitter_1_ld_st));
  Multiplexer #(.width(18), .enable("false")) multiplexer_7 (
    .in0(register_file_1_readdata2), .out(multiplexer_7_out), .sel(data_splitter_1_opcode[2]));  // open: in1
  Multiplexer #(.width(18), .enable("false")) multiplexer_8 (
    .in0(register_file_1_readdata1), .out(multiplexer_8_out), .sel(data_splitter_1_opcode[2]));  // open: in1
  ALU alu_1 (
    .imm(data_splitter_1_extended_imm_val), .reg1input(multiplexer_7_out), .reg_imm(data_splitter_1_imm_reg),
    .reg2input(multiplexer_8_out), .loadALU(control_unit_1_loadalu), .clck(clock_1_out),
    .selectoper({data_splitter_1_opcode[1], data_splitter_1_opcode[2]}), .\output (alu_1_output));
  RAM #(.addrWidth(10), .dataWidth(18), .bus("separate")) ram_1 (
    .addr(multiplexer_6_out), .din(register_file_1_readdata2), .data(ram_1_data),
    .str(control_unit_1_mem_store), .sel(control_unit_1_active_mem), .clk(clock_1_out),
    .ld(control_unit_1_load_mem), .clr(in_4));

  // Notes on the sheet:
  //   Reset Data Memory
  //   Comparator
  //   Clock
  //   Instruction Memory
  //   contents of rom_1 (hex, n*v repeats v):
  //   1554b 17741 17ec0 16f40 1768f 3a9a3 14cc1 37ffb 2800f 2801f 22800 28035
  //   Register File
  //   Data Memory
endmodule

// alu
module ALU (
  input  [17:0] imm,
  input  [17:0] reg1input,
  input  reg_imm,
  input  [17:0] reg2input,
  input  loadALU,
  input  clck,
  input  [1:0] selectoper,
  output [17:0] \output 
);

  wire [17:0] adder_or_subs_1_output, and_1_out, multiplexer_1_out, or_1_out, reg1_q, reg2_q, xor_1_out;

  Multiplexer #(.width(18), .enable("false")) multiplexer_1 (
    .in0(reg1input), .in1(imm), .out(multiplexer_1_out), .sel(reg_imm));
  Register #(.width(18)) reg1 (.D(multiplexer_1_out), .en(loadALU), .Q(reg1_q), .clk(clck));  // open: clr
  Register #(.width(18)) reg2 (.D(reg2input), .en(loadALU), .Q(reg2_q), .clk(clck));  // open: clr
  adder_or_subs adder_or_subs_1 (.input_1(reg2_q), .input_2(reg1_q), .\output (adder_or_subs_1_output));
  assign and_1_out = reg1_q & reg2_q;  // AND_Gate and_1, 18 bits wide
  assign or_1_out = reg1_q | reg2_q;  // OR_Gate or_1, 18 bits wide
  assign xor_1_out = reg1_q ^ reg2_q;  // XOR_Gate xor_1, 18 bits wide
  Multiplexer #(.select(2), .width(18), .enable("false")) multiplexer_2 (
    .in0(and_1_out), .in1(or_1_out), .in2(adder_or_subs_1_output), .in3(xor_1_out), .out(\output ),
    .sel(selectoper));
endmodule

// register file
module Register_file (
  input  [17:0] writeData,
  input  [3:0] writeAdress,
  input  readEN,
  input  [3:0] readADD1,
  input  writeEnable,
  input  [3:0] readADD2,
  input  clck,
  input  clear,
  output [17:0] readDATA1,
  output [17:0] readDATA2
);

  wire and_1_out, and_2_out, and_3_out, and_4_out, and_5_out, and_6_out, and_7_out, and_8_out, and_9_out,
       and_10_out, and_11_out, and_12_out, and_13_out, and_14_out, and_15_out, and_16_out, decoder_1_out0,
       decoder_1_out1, decoder_1_out2, decoder_1_out3, decoder_1_out4, decoder_1_out5, decoder_1_out6,
       decoder_1_out7, decoder_1_out8, decoder_1_out9, decoder_1_out10, decoder_1_out11, decoder_1_out12,
       decoder_1_out13, decoder_1_out14, decoder_1_out15, decoder_2_out0, decoder_2_out1, decoder_2_out2,
       decoder_2_out3, decoder_2_out4, decoder_2_out5, decoder_2_out6, decoder_2_out7, decoder_2_out8,
       decoder_2_out9, decoder_2_out10, decoder_2_out11, decoder_2_out12, decoder_2_out13, decoder_2_out14,
       decoder_2_out15, decoder_3_out0, decoder_3_out1, decoder_3_out2, decoder_3_out3, decoder_3_out4,
       decoder_3_out5, decoder_3_out6, decoder_3_out7, decoder_3_out8, decoder_3_out9, decoder_3_out10,
       decoder_3_out11, decoder_3_out12, decoder_3_out13, decoder_3_out14, decoder_3_out15;
  wire [17:0] buffer_1_out, buffer_2_out, buffer_3_out, buffer_4_out, buffer_5_out, buffer_6_out,
       buffer_7_out, buffer_8_out, buffer_9_out, buffer_10_out, buffer_11_out, buffer_12_out, buffer_13_out,
       buffer_14_out, buffer_15_out, register_1_q, register_2_q, register_3_q, register_4_q, register_5_q,
       register_6_q, register_7_q, register_8_q, register_9_q, register_10_q, register_11_q, register_12_q,
       register_13_q, register_14_q, register_15_q, register_16_q;

  Decoder #(.select(4), .disabled(0)) decoder_1 (
    .out0(decoder_1_out0), .out1(decoder_1_out1), .out2(decoder_1_out2), .out3(decoder_1_out3),
    .out4(decoder_1_out4), .out5(decoder_1_out5), .out6(decoder_1_out6), .out7(decoder_1_out7),
    .out8(decoder_1_out8), .out9(decoder_1_out9), .out10(decoder_1_out10), .out11(decoder_1_out11),
    .out12(decoder_1_out12), .out13(decoder_1_out13), .out14(decoder_1_out14), .out15(decoder_1_out15),
    .sel(writeAdress), .en(writeEnable));
  and and_1 (and_1_out, decoder_1_out0, writeEnable);
  and and_2 (and_2_out, decoder_1_out1, writeEnable);
  and and_3 (and_3_out, decoder_1_out2, writeEnable);
  and and_4 (and_4_out, decoder_1_out3, writeEnable);
  and and_5 (and_5_out, decoder_1_out4, writeEnable);
  and and_6 (and_6_out, decoder_1_out5, writeEnable);
  and and_7 (and_7_out, decoder_1_out6, writeEnable);
  and and_8 (and_8_out, decoder_1_out7, writeEnable);
  and and_9 (and_9_out, decoder_1_out8, writeEnable);
  and and_10 (and_10_out, decoder_1_out9, writeEnable);
  and and_11 (and_11_out, decoder_1_out10, writeEnable);
  and and_12 (and_12_out, decoder_1_out11, writeEnable);
  and and_13 (and_13_out, decoder_1_out12, writeEnable);
  and and_14 (and_14_out, decoder_1_out13, writeEnable);
  and and_15 (and_15_out, decoder_1_out14, writeEnable);
  and and_16 (and_16_out, decoder_1_out15, writeEnable);
  assign buffer_1_out = buffer_2_out;  // Buffer buffer_1, 18 bits wide
  assign buffer_2_out = buffer_3_out;  // Buffer buffer_2, 18 bits wide
  assign buffer_3_out = buffer_4_out;  // Buffer buffer_3, 18 bits wide
  assign buffer_4_out = writeData;  // Buffer buffer_4, 18 bits wide
  assign buffer_5_out = writeData;  // Buffer buffer_5, 18 bits wide
  assign buffer_6_out = buffer_5_out;  // Buffer buffer_6, 18 bits wide
  assign buffer_7_out = buffer_6_out;  // Buffer buffer_7, 18 bits wide
  assign buffer_8_out = buffer_7_out;  // Buffer buffer_8, 18 bits wide
  assign buffer_9_out = buffer_8_out;  // Buffer buffer_9, 18 bits wide
  assign buffer_10_out = buffer_9_out;  // Buffer buffer_10, 18 bits wide
  assign buffer_11_out = buffer_10_out;  // Buffer buffer_11, 18 bits wide
  assign buffer_12_out = buffer_11_out;  // Buffer buffer_12, 18 bits wide
  assign buffer_13_out = buffer_12_out;  // Buffer buffer_13, 18 bits wide
  assign buffer_14_out = buffer_13_out;  // Buffer buffer_14, 18 bits wide
  assign buffer_15_out = buffer_14_out;  // Buffer buffer_15, 18 bits wide
  Register #(.width(18)) register_1 (.D(buffer_1_out), .en(and_1_out), .Q(register_1_q), .clk(clck), .clr(clear));
  Register #(.width(18)) register_2 (.D(buffer_2_out), .en(and_2_out), .Q(register_2_q), .clk(clck), .clr(clear));
  Register #(.width(18)) register_3 (.D(buffer_3_out), .en(and_3_out), .Q(register_3_q), .clk(clck), .clr(clear));
  Register #(.width(18)) register_4 (.D(buffer_4_out), .en(and_4_out), .Q(register_4_q), .clk(clck), .clr(clear));
  Register #(.width(18)) register_5 (.D(writeData), .en(and_5_out), .Q(register_5_q), .clk(clck), .clr(clear));
  Register #(.width(18)) register_6 (.D(buffer_5_out), .en(and_6_out), .Q(register_6_q), .clk(clck), .clr(clear));
  Register #(.width(18)) register_7 (.D(buffer_6_out), .en(and_7_out), .Q(register_7_q), .clk(clck), .clr(clear));
  Register #(.width(18)) register_8 (.D(buffer_7_out), .en(and_8_out), .Q(register_8_q), .clk(clck), .clr(clear));
  Register #(.width(18)) register_9 (.D(buffer_8_out), .en(and_9_out), .Q(register_9_q), .clk(clck), .clr(clear));
  Register #(.width(18)) register_10 (.D(buffer_9_out), .en(and_10_out), .Q(register_10_q), .clk(clck), .clr(clear));
  Register #(.width(18)) register_11 (.D(buffer_10_out), .en(and_11_out), .Q(register_11_q), .clk(clck), .clr(clear));
  Register #(.width(18)) register_12 (.D(buffer_11_out), .en(and_12_out), .Q(register_12_q), .clk(clck), .clr(clear));
  Register #(.width(18)) register_13 (.D(buffer_12_out), .en(and_13_out), .Q(register_13_q), .clk(clck), .clr(clear));
  Register #(.width(18)) register_14 (.D(buffer_13_out), .en(and_14_out), .Q(register_14_q), .clk(clck), .clr(clear));
  Register #(.width(18)) register_15 (.D(buffer_14_out), .en(and_15_out), .Q(register_15_q), .clk(clck), .clr(clear));
  Register #(.width(18)) register_16 (.D(buffer_15_out), .en(and_16_out), .Q(register_16_q), .clk(clck), .clr(clear));
  assign readDATA1 = decoder_2_out0 ? register_1_q : 18'bz;  // Controlled_Buffer controlled_buffer_1
  assign readDATA2 = decoder_3_out0 ? register_1_q : 18'bz;  // Controlled_Buffer controlled_buffer_2
  assign readDATA1 = decoder_2_out1 ? register_2_q : 18'bz;  // Controlled_Buffer controlled_buffer_3
  assign readDATA2 = decoder_3_out1 ? register_2_q : 18'bz;  // Controlled_Buffer controlled_buffer_4
  assign readDATA1 = decoder_2_out2 ? register_3_q : 18'bz;  // Controlled_Buffer controlled_buffer_5
  assign readDATA2 = decoder_3_out2 ? register_3_q : 18'bz;  // Controlled_Buffer controlled_buffer_6
  assign readDATA1 = decoder_2_out3 ? register_4_q : 18'bz;  // Controlled_Buffer controlled_buffer_7
  assign readDATA2 = decoder_3_out3 ? register_4_q : 18'bz;  // Controlled_Buffer controlled_buffer_8
  assign readDATA1 = decoder_2_out4 ? register_5_q : 18'bz;  // Controlled_Buffer controlled_buffer_9
  assign readDATA2 = decoder_3_out4 ? register_5_q : 18'bz;  // Controlled_Buffer controlled_buffer_10
  assign readDATA1 = decoder_2_out5 ? register_6_q : 18'bz;  // Controlled_Buffer controlled_buffer_11
  assign readDATA2 = decoder_3_out5 ? register_6_q : 18'bz;  // Controlled_Buffer controlled_buffer_12
  assign readDATA1 = decoder_2_out6 ? register_7_q : 18'bz;  // Controlled_Buffer controlled_buffer_13
  assign readDATA2 = decoder_3_out6 ? register_7_q : 18'bz;  // Controlled_Buffer controlled_buffer_14
  assign readDATA1 = decoder_2_out7 ? register_8_q : 18'bz;  // Controlled_Buffer controlled_buffer_15
  assign readDATA2 = decoder_3_out7 ? register_8_q : 18'bz;  // Controlled_Buffer controlled_buffer_16
  assign readDATA1 = decoder_2_out8 ? register_9_q : 18'bz;  // Controlled_Buffer controlled_buffer_17
  assign readDATA2 = decoder_3_out8 ? register_9_q : 18'bz;  // Controlled_Buffer controlled_buffer_18
  assign readDATA1 = decoder_2_out9 ? register_10_q : 18'bz;  // Controlled_Buffer controlled_buffer_19
  assign readDATA2 = decoder_3_out9 ? register_10_q : 18'bz;  // Controlled_Buffer controlled_buffer_20
  assign readDATA1 = decoder_2_out10 ? register_11_q : 18'bz;  // Controlled_Buffer controlled_buffer_21
  assign readDATA2 = decoder_3_out10 ? register_11_q : 18'bz;  // Controlled_Buffer controlled_buffer_22
  assign readDATA1 = decoder_2_out11 ? register_12_q : 18'bz;  // Controlled_Buffer controlled_buffer_23
  assign readDATA2 = decoder_3_out11 ? register_12_q : 18'bz;  // Controlled_Buffer controlled_buffer_24
  assign readDATA1 = decoder_2_out12 ? register_13_q : 18'bz;  // Controlled_Buffer controlled_buffer_25
  assign readDATA2 = decoder_3_out12 ? register_13_q : 18'bz;  // Controlled_Buffer controlled_buffer_26
  assign readDATA1 = decoder_2_out13 ? register_14_q : 18'bz;  // Controlled_Buffer controlled_buffer_27
  assign readDATA2 = decoder_3_out13 ? register_14_q : 18'bz;  // Controlled_Buffer controlled_buffer_28
  assign readDATA1 = decoder_2_out14 ? register_15_q : 18'bz;  // Controlled_Buffer controlled_buffer_29
  assign readDATA2 = decoder_3_out14 ? register_15_q : 18'bz;  // Controlled_Buffer controlled_buffer_30
  assign readDATA1 = decoder_2_out15 ? register_16_q : 18'bz;  // Controlled_Buffer controlled_buffer_31
  assign readDATA2 = decoder_3_out15 ? register_16_q : 18'bz;  // Controlled_Buffer controlled_buffer_32
  Decoder #(.select(4)) decoder_2 (
    .out0(decoder_2_out0), .out1(decoder_2_out1), .out2(decoder_2_out2), .out3(decoder_2_out3),
    .out4(decoder_2_out4), .out5(decoder_2_out5), .out6(decoder_2_out6), .out7(decoder_2_out7),
    .out8(decoder_2_out8), .out9(decoder_2_out9), .out10(decoder_2_out10), .out11(decoder_2_out11),
    .out12(decoder_2_out12), .out13(decoder_2_out13), .out14(decoder_2_out14), .out15(decoder_2_out15),
    .sel(readADD1), .en(readEN));
  Decoder #(.select(4)) decoder_3 (
    .out0(decoder_3_out0), .out1(decoder_3_out1), .out2(decoder_3_out2), .out3(decoder_3_out3),
    .out4(decoder_3_out4), .out5(decoder_3_out5), .out6(decoder_3_out6), .out7(decoder_3_out7),
    .out8(decoder_3_out8), .out9(decoder_3_out9), .out10(decoder_3_out10), .out11(decoder_3_out11),
    .out12(decoder_3_out12), .out13(decoder_3_out13), .out14(decoder_3_out14), .out15(decoder_3_out15),
    .sel(readADD2), .en(readEN));
endmodule

module PC (
  input  clear,
  input  [17:0] PCinDATA,
  input  clck,
  input  loadEnable,
  output [17:0] PCoutput
);

  Register #(.width(18)) register_1 (.D(PCinDATA), .en(loadEnable), .Q(PCoutput), .clk(clck), .clr(clear));
endmodule

// Control unit
module Control_Unit (
  input  iftrue,
  input  [2:0] opcode,
  input  clear,
  input  clock,
  output [3:0] next,
  output [3:0] current,
  output pc_write,
  output loadALU,
  output write_enable,
  output load_mem,
  output fetch,
  output mem_store,
  output active_mem,
  output read_en,
  output jump
);

  wire and_1_out, and_2_out, and_3_out, and_4_out, and_5_out, and_6_out, and_7_out, and_8_out, and_9_out,
       and_10_out, and_11_out, and_12_out, and_13_out, and_14_out, and_16_out, and_17_out, and_18_out,
       and_19_out, and_20_out, and_24_out, and_25_out, and_27_out, and_29_out, and_30_out, and_31_out,
       and_32_out, not_1_out, not_2_out, not_3_out, not_4_out, not_5_out, not_6_out, not_7_out, not_8_out,
       not_9_out, not_10_out, not_11_out, not_12_out, not_13_out, not_14_out, not_15_out, not_16_out,
       not_17_out, not_18_out, not_19_out, not_20_out, not_21_out, not_22_out, not_23_out, not_24_out,
       not_25_out, not_26_out, not_27_out, not_28_out, not_29_out, not_30_out, not_31_out, not_33_out,
       not_34_out, not_35_out, not_36_out, not_37_out, not_38_out, not_39_out, not_40_out, not_41_out,
       not_42_out, not_43_out, not_44_out, not_45_out;

  not not_1 (not_1_out, current[3]);
  not not_2 (not_2_out, current[2]);
  not not_3 (not_3_out, current[1]);
  not not_4 (not_4_out, current[0]);
  not not_5 (not_5_out, current[3]);
  not not_6 (not_6_out, current[2]);
  not not_7 (not_7_out, current[1]);
  not not_8 (not_8_out, opcode[1]);
  not not_9 (not_9_out, current[0]);
  not not_10 (not_10_out, current[3]);
  not not_11 (not_11_out, current[2]);
  not not_12 (not_12_out, current[1]);
  not not_13 (not_13_out, current[0]);
  not not_14 (not_14_out, current[3]);
  not not_15 (not_15_out, current[2]);
  not not_16 (not_16_out, current[1]);
  not not_17 (not_17_out, opcode[2]);
  not not_18 (not_18_out, current[0]);
  and and_1 (and_1_out, not_1_out, not_2_out, not_3_out, current[0], opcode[2], opcode[1]);
  and and_2 (and_2_out, not_1_out, not_2_out, current[1], not_4_out);
  and and_3 (and_3_out, current[3], not_2_out, not_3_out, current[0]);
  and and_4 (and_4_out, not_5_out, not_6_out, not_7_out, current[0], opcode[2], not_8_out);
  and and_5 (and_5_out, not_5_out, current[2], not_9_out);
  not not_19 (not_19_out, opcode[1]);
  not not_20 (not_20_out, iftrue);
  or or_1 (next[3], and_1_out, and_2_out, and_3_out);
  or or_2 (next[2], and_4_out, and_5_out);
  and and_6 (and_6_out, not_14_out, not_15_out, not_16_out, current[0], not_17_out);
  and and_7 (and_7_out, not_14_out, not_15_out, not_16_out, current[0], opcode[2], not_19_out, opcode[0]);
  and and_8 (and_8_out, not_14_out, current[1], not_18_out);
  and and_9 (and_9_out, current[3], not_15_out, current[1], current[0]);
  and and_10 (and_10_out, current[3], not_15_out, not_16_out, current[0], not_20_out);
  and and_11 (and_11_out, current[3], not_11_out, current[1], current[0]);
  and and_12 (and_12_out, not_10_out, not_11_out, not_13_out);
  and and_13 (and_13_out, not_10_out, current[2], not_13_out);
  and and_14 (and_14_out, not_10_out, not_11_out, not_12_out, current[0], opcode[2], opcode[1], opcode[0]);
  or or_3 (next[1], and_6_out, and_7_out, and_8_out, and_9_out, and_10_out);
  or or_4 (next[0], and_11_out, and_12_out, and_13_out, and_14_out);
  not not_21 (not_21_out, current[1]);
  not not_22 (not_22_out, current[3]);
  not not_23 (not_23_out, current[3]);
  not not_24 (not_24_out, current[2]);
  not not_25 (not_25_out, current[1]);
  not not_26 (not_26_out, current[0]);
  not not_27 (not_27_out, current[3]);
  not not_28 (not_28_out, current[2]);
  not not_29 (not_29_out, current[0]);
  not not_30 (not_30_out, current[3]);
  not not_31 (not_31_out, current[2]);
  // NOT_Gate not_32 has open pins: in=current[0], out=open
  not not_33 (not_33_out, current[3]);
  not not_34 (not_34_out, current[1]);
  not not_35 (not_35_out, current[3]);
  not not_36 (not_36_out, current[2]);
  not not_37 (not_37_out, current[1]);
  not not_38 (not_38_out, current[3]);
  and and_15 (active_mem, not_22_out, current[2]);
  not not_39 (not_39_out, current[3]);
  not not_40 (not_40_out, current[2]);
  not not_41 (not_41_out, current[1]);
  not not_42 (not_42_out, current[0]);
  not not_43 (not_43_out, current[2]);
  not not_44 (not_44_out, current[1]);
  not not_45 (not_45_out, current[0]);
  Register #(.width(4)) register_1 (.D(next), .Q(current), .clk(clock), .clr(clear));  // open: en
  and and_16 (and_16_out, not_27_out, not_28_out, current[1], not_29_out);
  and and_17 (and_17_out, current[3], not_28_out, current[1], current[0]);
  and and_18 (and_18_out, not_30_out, not_31_out, current[1], current[0]);
  and and_19 (and_19_out, not_30_out, current[2], not_21_out);
  and and_20 (and_20_out, current[3], not_31_out, current[1], current[0]);
  and and_21 (load_mem, not_33_out, current[2], not_34_out);
  and and_22 (fetch, not_35_out, not_36_out, current[1], not_37_out);
  and and_23 (jump, current[3], not_43_out, not_44_out, not_45_out);
  and and_24 (and_24_out, not_23_out, current[2], current[0]);
  and and_25 (and_25_out, current[3], not_24_out, not_26_out);
  // AND_Gate and_26 has open pins: in0=not_23_out, in1=not_24_out, in2=not_25_out, in3=not_26_out, out=open
  and and_27 (and_27_out, not_23_out, not_24_out, current[1], current[0]);
  or or_5 (loadALU, and_16_out, and_17_out);
  or or_6 (write_enable, and_18_out, and_19_out, and_20_out);
  and and_28 (mem_store, not_38_out, current[2], current[1]);
  and and_29 (and_29_out, not_39_out, current[2], current[1]);
  and and_30 (and_30_out, not_39_out, not_40_out, current[1], not_42_out);
  and and_31 (and_31_out, current[3], not_40_out, not_41_out);
  and and_32 (and_32_out, current[3], not_40_out, current[1]);
  or or_7 (pc_write, and_24_out, and_25_out, and_27_out);
  or or_8 (read_en, and_29_out, and_30_out, and_31_out, and_32_out);

  // Other names for the same wires on the sheet: s3 = current[0]; s2 = current[1]; s1 = current[2]; s0 = current[3];
  //   if = iftrue; n3 = next[0]; n2 = next[1]; n1 = next[2]; n0 = next[3]; _15 = opcode[0]; _16 = opcode[1];
  //   _17 = opcode[2]
endmodule

module _18_bit_comparator (
  input  [17:0] input_1,
  input  [17:0] input_2,
  output equal,
  output greater,
  output less
);

  wire and_2_out, and_3_out, n2_bit_comparator_1_equal, n2_bit_comparator_1_greater,
       n2_bit_comparator_1_less, n16bit_comparator_1_equal, n16bit_comparator_1_greater,
       n16bit_comparator_1_less;

  _16bit_comparator u_16bit_comparator_1 (
    .input_1(input_1[15:0]), .input_2(input_2[15:0]), .equal(n16bit_comparator_1_equal),
    .greater(n16bit_comparator_1_greater), .less(n16bit_comparator_1_less));
  _2_bit_comparator u_2_bit_comparator_1 (
    .input_1(input_1[17:16]), .input_2(input_2[17:16]), .equal(n2_bit_comparator_1_equal),
    .greater(n2_bit_comparator_1_greater), .less(n2_bit_comparator_1_less));
  and and_1 (equal, n16bit_comparator_1_equal, n2_bit_comparator_1_equal);
  and and_2 (and_2_out, n2_bit_comparator_1_equal, n16bit_comparator_1_greater);
  and and_3 (and_3_out, n2_bit_comparator_1_equal, n16bit_comparator_1_less);
  or or_1 (greater, and_2_out, n2_bit_comparator_1_greater);
  or or_2 (less, and_3_out, n2_bit_comparator_1_less);
endmodule

module _2_bit_comparator (
  input  [1:0] input_1,
  input  [1:0] input_2,
  output equal,
  output greater,
  output less
);

  wire and_1_out, and_2_out, and_3_out, and_4_out, not_1_out, not_2_out, not_3_out, not_4_out, xnor_1_out,
       xnor_2_out;

  xnor xnor_1 (xnor_1_out, input_1[1], input_2[1]);
  xnor xnor_2 (xnor_2_out, input_1[0], input_2[0]);
  and and_1 (and_1_out, xnor_1_out, input_1[0], not_1_out);
  not not_1 (not_1_out, input_2[0]);
  not not_2 (not_2_out, input_2[1]);
  and and_2 (and_2_out, not_2_out, input_1[1]);
  and and_3 (and_3_out, xnor_1_out, input_2[0], not_3_out);
  not not_3 (not_3_out, input_1[0]);
  and and_4 (and_4_out, input_2[1], not_4_out);
  not not_4 (not_4_out, input_1[1]);
  and and_5 (equal, xnor_1_out, xnor_2_out);
  or or_1 (greater, and_1_out, and_2_out);
  or or_2 (less, and_3_out, and_4_out);
endmodule

module _4_bit_comparator (
  input  [3:0] input_1,
  input  [3:0] input_2,
  output equal,
  output greater,
  output less
);

  wire _0_1_equal, _0_1_greater, _0_1_less, _2_3_equal, _2_3_greater, _2_3_less, and_2_out, and_3_out;

  _2_bit_comparator _0_1 (
    .input_1(input_1[1:0]), .input_2(input_2[1:0]), .equal(_0_1_equal), .greater(_0_1_greater),
    .less(_0_1_less));
  _2_bit_comparator _2_3 (
    .input_1(input_1[3:2]), .input_2(input_2[3:2]), .equal(_2_3_equal), .greater(_2_3_greater),
    .less(_2_3_less));
  and and_1 (equal, _0_1_equal, _2_3_equal);
  and and_2 (and_2_out, _2_3_equal, _0_1_greater);
  and and_3 (and_3_out, _2_3_equal, _0_1_less);
  or or_1 (greater, and_2_out, _2_3_greater);
  or or_2 (less, and_3_out, _2_3_less);
endmodule

module _8_bit_comparator (
  input  [7:0] input_1,
  input  [7:0] input_2,
  output equal,
  output greater,
  output less
);

  wire and_2_out, and_3_out, n4_bit_comparator_1_equal, n4_bit_comparator_1_greater,
       n4_bit_comparator_1_less, n4_bit_comparator_2_equal, n4_bit_comparator_2_greater,
       n4_bit_comparator_2_less;

  _4_bit_comparator u_4_bit_comparator_1 (
    .input_1(input_1[3:0]), .input_2(input_2[3:0]), .equal(n4_bit_comparator_1_equal),
    .greater(n4_bit_comparator_1_greater), .less(n4_bit_comparator_1_less));
  _4_bit_comparator u_4_bit_comparator_2 (
    .input_1(input_1[7:4]), .input_2(input_2[7:4]), .equal(n4_bit_comparator_2_equal),
    .greater(n4_bit_comparator_2_greater), .less(n4_bit_comparator_2_less));
  and and_1 (equal, n4_bit_comparator_1_equal, n4_bit_comparator_2_equal);
  and and_2 (and_2_out, n4_bit_comparator_2_equal, n4_bit_comparator_1_greater);
  and and_3 (and_3_out, n4_bit_comparator_2_equal, n4_bit_comparator_1_less);
  or or_1 (greater, and_2_out, n4_bit_comparator_2_greater);
  or or_2 (less, and_3_out, n4_bit_comparator_2_less);
endmodule

module _16bit_comparator (
  input  [15:0] input_1,
  input  [15:0] input_2,
  output equal,
  output greater,
  output less
);

  wire and_2_out, and_3_out, n8_bit_comparator_1_equal, n8_bit_comparator_1_greater,
       n8_bit_comparator_1_less, n8_bit_comparator_2_equal, n8_bit_comparator_2_greater,
       n8_bit_comparator_2_less;

  _8_bit_comparator u_8_bit_comparator_1 (
    .input_1(input_1[7:0]), .input_2(input_2[7:0]), .equal(n8_bit_comparator_1_equal),
    .greater(n8_bit_comparator_1_greater), .less(n8_bit_comparator_1_less));
  _8_bit_comparator u_8_bit_comparator_2 (
    .input_1(input_1[15:8]), .input_2(input_2[15:8]), .equal(n8_bit_comparator_2_equal),
    .greater(n8_bit_comparator_2_greater), .less(n8_bit_comparator_2_less));
  and and_1 (equal, n8_bit_comparator_1_equal, n8_bit_comparator_2_equal);
  and and_2 (and_2_out, n8_bit_comparator_2_equal, n8_bit_comparator_1_greater);
  and and_3 (and_3_out, n8_bit_comparator_2_equal, n8_bit_comparator_1_less);
  or or_1 (greater, and_2_out, n8_bit_comparator_2_greater);
  or or_2 (less, and_3_out, n8_bit_comparator_2_less);
endmodule

module branch (
  input  [2:0] nzp,
  input  [17:0] input_1,
  input  [17:0] input_2,
  output iftrue
);

  wire and_1_out, and_2_out, and_3_out, n18_bit_comparator_1_equal, n18_bit_comparator_1_greater,
       n18_bit_comparator_1_less;

  _18_bit_comparator u_18_bit_comparator_1 (
    .input_1(input_1), .input_2(input_2), .equal(n18_bit_comparator_1_equal),
    .greater(n18_bit_comparator_1_greater), .less(n18_bit_comparator_1_less));
  and and_1 (and_1_out, nzp[0], n18_bit_comparator_1_greater);
  and and_2 (and_2_out, nzp[1], n18_bit_comparator_1_equal);
  and and_3 (and_3_out, nzp[2], n18_bit_comparator_1_less);
  or or_1 (iftrue, and_1_out, and_2_out, and_3_out);
endmodule

module data_splitter (
  input  [17:0] input_18bit,
  output [2:0] opcode,
  output [3:0] write_reg,
  output [3:0] read_reg_1,
  output imm_reg,
  output [3:0] read_reg_2,
  output [17:0] extended_imm_val,
  output [9:0] ldadress,
  output [9:0] st_adress,
  output [17:0] jump_adrress,
  output [2:0] n_z_p,
  output [17:0] brach_adress,
  output ld_st,
  output branch_oper,
  output branch_or_jump
);

  wire and_1_out, and_2_out, and_3_out, and_4_out, and_5_out, and_7_out, and_8_out, and_9_out, and_10_out,
       not_1_out, not_2_out, not_3_out, not_4_out, not_5_out, not_6_out, not_7_out, not_8_out, not_9_out,
       not_10_out, not_11_out, not_12_out, not_13_out, not_14_out, or_1_out, or_2_out, or_3_out;
  wire [3:0] multiplexer_6_out;
  wire [5:0] multiplexer_3_out;
  wire [10:0] multiplexer_4_out, multiplexer_8_out;
  wire [14:0] multiplexer_9_out;

  or or_1 (or_1_out, not_1_out, and_1_out);
  or or_2 (or_2_out, not_2_out, and_2_out);
  not not_1 (not_1_out, input_18bit[17]);
  not not_2 (not_2_out, input_18bit[17]);
  and and_1 (and_1_out, input_18bit[17], not_3_out, not_4_out);
  and and_2 (and_2_out, input_18bit[17], not_5_out, input_18bit[15]);
  and and_3 (and_3_out, input_18bit[17], not_6_out, not_7_out);
  and and_4 (and_4_out, input_18bit[17], not_8_out, input_18bit[15]);
  and and_5 (and_5_out, input_18bit[17], input_18bit[16], not_9_out);
  and and_6 (branch_oper, input_18bit[17], input_18bit[16], input_18bit[15]);
  not not_3 (not_3_out, input_18bit[16]);
  not not_4 (not_4_out, input_18bit[15]);
  not not_5 (not_5_out, input_18bit[16]);
  not not_6 (not_6_out, input_18bit[16]);
  not not_7 (not_7_out, input_18bit[15]);
  not not_8 (not_8_out, input_18bit[16]);
  not not_9 (not_9_out, input_18bit[15]);
  not not_10 (not_10_out, input_18bit[16]);
  not not_11 (not_11_out, input_18bit[16]);
  not not_12 (not_12_out, input_18bit[16]);
  not not_13 (not_13_out, input_18bit[15]);
  and and_7 (and_7_out, input_18bit[17], not_10_out, not_11_out);
  and and_8 (and_8_out, input_18bit[17], not_12_out, input_18bit[15]);
  not not_14 (not_14_out, input_18bit[17]);
  and and_9 (and_9_out, input_18bit[17], input_18bit[16], not_13_out);
  or or_3 (or_3_out, and_7_out, and_8_out);
  Multiplexer #(.width(4), .enable("false")) multiplexer_1 (
    .in1(input_18bit[14:11]), .out(write_reg), .sel(or_1_out));  // open: in0
  Multiplexer #(.width(4), .enable("false")) multiplexer_2 (
    .in0(input_18bit[10:7]), .in1(input_18bit[11:8]), .out(read_reg_1), .sel(input_18bit[17]));
  and and_10 (and_10_out, input_18bit[6], not_14_out);
  and and_11 (ld_st, or_3_out, input_18bit[15]);
  Multiplexer #(.width(6), .enable("false")) multiplexer_3 (
    .in1(input_18bit[5:0]), .out(multiplexer_3_out), .sel(and_10_out));  // open: in0
  Multiplexer #(.width(11), .enable("false")) multiplexer_4 (
    .in1(input_18bit[10:0]), .out(multiplexer_4_out), .sel(and_3_out));  // open: in0
  Multiplexer #(.width(3), .enable("false")) multiplexer_5 (
    .in1(input_18bit[14:12]), .out(n_z_p), .sel(branch_oper));  // open: in0
  Multiplexer #(.width(4), .enable("false")) multiplexer_6 (
    .in1(input_18bit[3:0]), .out(multiplexer_6_out), .sel(branch_oper));  // open: in0
  Multiplexer #(.width(4), .enable("false")) multiplexer_7 (
    .in0(input_18bit[7:4]), .in1(input_18bit[3:0]), .out(read_reg_2), .sel(or_2_out));
  Bit_Extender #(.in_width(11), .out_width(10)) bit_extender_1 (.in(multiplexer_4_out), .out(ldadress));
  Multiplexer #(.width(11), .enable("false")) multiplexer_8 (
    .in1(input_18bit[14:4]), .out(multiplexer_8_out), .sel(and_4_out));  // open: in0
  Multiplexer #(.width(15), .enable("false")) multiplexer_9 (
    .in1(input_18bit[14:0]), .out(multiplexer_9_out), .sel(and_5_out));  // open: in0
  or or_4 (branch_or_jump, branch_oper, and_9_out);
  imm_extender imm_extender_1 (.imm_input(multiplexer_3_out), .extended(extended_imm_val));
  branch_extender branch_extender_1 (.branch_adress(multiplexer_6_out), .extended(brach_adress));
  Bit_Extender #(.in_width(11), .out_width(10)) bit_extender_2 (.in(multiplexer_8_out), .out(st_adress));
  jump_extender jump_extender_1 (.jump_adress(multiplexer_9_out), .extended(jump_adrress));

  assign imm_reg = input_18bit[6];
  assign opcode = input_18bit[17:15];
endmodule

module imm_extender (
  input  [5:0] imm_input,
  output [17:0] extended
);


  assign extended = {{13{imm_input[5]}}, imm_input[4:0]};
endmodule

module _18_bit_adder (
  input  c_in,
  input  [17:0] input_1,
  input  [17:0] input_2,
  output [17:0] utput,
  output c_out
);

  wire n16_bit_adder_1_c_out;

  _16_bit_adder u_16_bit_adder_1 (
    .c_in(c_in), .input_1(input_1[15:0]), .input_2(input_2[15:0]), .utput(utput[15:0]),
    .c_out(n16_bit_adder_1_c_out));
  _2_bit_adder u_2_bit_adder_1 (
    .cin(n16_bit_adder_1_c_out), .input_1(input_1[17:16]), .input_2(input_2[17:16]), .\output (utput[17:16]),
    .cout(c_out));
endmodule

module _2_bit_adder (
  input  cin,
  input  [1:0] input_1,
  input  [1:0] input_2,
  output [1:0] \output ,
  output cout
);

  wire and_1_out, and_2_out, and_3_out, and_4_out, or_1_out, xor_1_out, xor_2_out;

  xor xor_1 (xor_1_out, input_1[0], input_2[0]);
  xor xor_2 (xor_2_out, input_1[1], input_2[1]);
  xor xor_3 (\output [0], xor_1_out, cin);
  and and_1 (and_1_out, xor_1_out, cin);
  and and_2 (and_2_out, input_2[0], input_1[0]);
  xor xor_4 (\output [1], xor_2_out, or_1_out);
  and and_3 (and_3_out, xor_2_out, or_1_out);
  and and_4 (and_4_out, input_2[1], input_1[1]);
  or or_1 (or_1_out, and_1_out, and_2_out);
  or or_2 (cout, and_3_out, and_4_out);
endmodule

module _4_bit_adder (
  input  c_in,
  input  [3:0] input_1,
  input  [3:0] input_2,
  output [3:0] utput,
  output c_out
);

  wire n2_bit_adder_1_cout;

  _2_bit_adder u_2_bit_adder_1 (
    .cin(c_in), .input_1(input_1[1:0]), .input_2(input_2[1:0]), .\output (utput[1:0]),
    .cout(n2_bit_adder_1_cout));
  _2_bit_adder u_2_bit_adder_2 (
    .cin(n2_bit_adder_1_cout), .input_1(input_1[3:2]), .input_2(input_2[3:2]), .\output (utput[3:2]),
    .cout(c_out));
endmodule

module _8_bit_adder (
  input  c_in,
  input  [7:0] input_1,
  input  [7:0] input_2,
  output [7:0] utput,
  output c_out
);

  wire n4_bit_adder_1_c_out;

  _4_bit_adder u_4_bit_adder_1 (
    .c_in(c_in), .input_1(input_1[3:0]), .input_2(input_2[3:0]), .utput(utput[3:0]),
    .c_out(n4_bit_adder_1_c_out));
  _4_bit_adder u_4_bit_adder_2 (
    .c_in(n4_bit_adder_1_c_out), .input_1(input_1[7:4]), .input_2(input_2[7:4]), .utput(utput[7:4]),
    .c_out(c_out));
endmodule

module _16_bit_adder (
  input  c_in,
  input  [15:0] input_1,
  input  [15:0] input_2,
  output [15:0] utput,
  output c_out
);

  wire n8_bit_adder_1_c_out;

  _8_bit_adder u_8_bit_adder_1 (
    .c_in(c_in), .input_1(input_1[7:0]), .input_2(input_2[7:0]), .utput(utput[7:0]),
    .c_out(n8_bit_adder_1_c_out));
  _8_bit_adder u_8_bit_adder_2 (
    .c_in(n8_bit_adder_1_c_out), .input_1(input_1[15:8]), .input_2(input_2[15:8]), .utput(utput[15:8]),
    .c_out(c_out));
endmodule

module sub (
  input  [17:0] input_1,
  input  [17:0] input_2,
  output [17:0] out
);

  wire [17:0] not_1_out;

  assign not_1_out = ~input_2;  // NOT_Gate not_1, 18 bits wide
  _18_bit_adder u_18_bit_adder_1 (.c_in(1'b1), .input_1(not_1_out), .input_2(input_1), .utput(out));  // open: c_out
endmodule

// add or sub
module adder_or_subs (
  input  [17:0] input_1,
  input  [17:0] input_2,
  output [17:0] \output 
);

  wire [17:0] n18_bit_adder_1_utput, sub_1_out;

  _18_bit_adder u_18_bit_adder_1 (
    .c_in(1'b0), .input_1(input_1), .input_2(input_2), .utput(n18_bit_adder_1_utput));  // open: c_out
  sub sub_1 (.input_1(input_1), .input_2(input_2), .out(sub_1_out));
  Multiplexer #(.width(18), .enable("false")) multiplexer_1 (
    .in0(n18_bit_adder_1_utput), .in1(sub_1_out), .out(\output ), .sel(input_2[17]));
endmodule

module branch_extender (
  input  [3:0] branch_adress,
  output [17:0] extended
);


  assign extended = {{15{branch_adress[3]}}, branch_adress[2:0]};
endmodule

module jump_extender (
  input  [14:0] jump_adress,
  output [17:0] extended
);


  assign extended = {{4{jump_adress[14]}}, jump_adress[13:0]};
endmodule
